# Fritzing sketch Circuit (saved by Fritzing 0.9.3b)
breadboards: 1

parts:
  Adafruit_HUZZAH_ESP8266_Breakout1 = Adafruit HUZZAH ESP8266 Breakout [part_number=2471]
  Part1 = Adafruit MMA8451 Accelerometer [part_number="Adafruit #2019"]
  VALVE1 = Plastic Solenoid Valve
  SD_card_module1 = SD_Card_Module.fzp
  BAT1 = Battery Holders [package=battery-aa]
  IC1 = Voltage Regulator LM1117 [package=sot223]
  Q2 = Basic FET N-Channel [package="TO220 [THT]"]
  D1 = Diode [package=diode-1n4001]
  R1 = Resistor [tolerance=±5% resistance=220 package="2512 [SMD]"]

nets:
  N1: Adafruit_HUZZAH_ESP8266_Breakout1.VBat, IC1.ADJ
  N2: Adafruit_HUZZAH_ESP8266_Breakout1.V+, SD_card_module1.connector2
  N3: Adafruit_HUZZAH_ESP8266_Breakout1.#13, SD_card_module1.connector5
  N4: Adafruit_HUZZAH_ESP8266_Breakout1.#12, SD_card_module1.connector6
  N5: Adafruit_HUZZAH_ESP8266_Breakout1.#16, R1.Pin_1
  N6: Adafruit_HUZZAH_ESP8266_Breakout1.#5, Part1.SDA
  N7: Adafruit_HUZZAH_ESP8266_Breakout1.#4, Part1.SCL
  N8: Adafruit_HUZZAH_ESP8266_Breakout1.#0, SD_card_module1.connector3
  N9: Adafruit_HUZZAH_ESP8266_Breakout1.#15, SD_card_module1.connector4
  N10: Adafruit_HUZZAH_ESP8266_Breakout1.GND, SD_card_module1.connector0
  N11: VALVE1.no_name_yet#1, Q2.drain
  N12: VALVE1.no_name_yet#2, BAT1.-, IC1.OUT, D1.A
  N13: BAT1.+, IC1.IN

custom parts:
  Adafruit MMA8451 Accelerometer: So many accelerometers and so little time! We've expanded our accelerometer selection even more with this high-precision and inexpensive MMA8451 Triple-Axis Accelerometer w/ 14-bit ADC. You can detect motion, tilt and basic orientation with a digital accelerometer - and the MMA8451 is a great accelerometer to start with. It has a wide usage range, from +-2g up to +-8g yet is easy to use with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
